// Logisim project controller.circ as structural Verilog: 1 circuit, main circuit main
module main (
);

  wire and_1_out, and_2_out, button_1_out, clock_1_out, dipswitch_37_p1, dipswitch_37_p2, dipswitch_37_p3,
       dipswitch_37_p4, dipswitch_37_p5, dipswitch_37_p6, dipswitch_37_p7, dipswitch_37_p8, dipswitch_38_p1,
       dipswitch_38_p2, dipswitch_38_p3, dipswitch_38_p4, dipswitch_38_p5, dipswitch_38_p6, dipswitch_38_p7,
       dipswitch_38_p8, dipswitch_38_p9, dipswitch_38_p10, dipswitch_39_p1, dipswitch_39_p2, dipswitch_39_p3,
       dipswitch_39_p4, dipswitch_39_p5, dipswitch_39_p6, dipswitch_39_p7, dipswitch_39_p8, dipswitch_39_p9,
       multiplexer_1_out, multiplexer_2_out, multiplexer_3_out, multiplexer_4_out, multiplexer_5_out,
       multiplexer_6_out, multiplexer_7_out, multiplexer_8_out, multiplexer_9_out, multiplexer_10_out,
       multiplexer_11_out, multiplexer_12_out, multiplexer_13_out, multiplexer_14_out, multiplexer_15_out,
       multiplexer_16_out, multiplexer_17_out, multiplexer_18_out, multiplexer_19_out, multiplexer_20_out,
       nand_1_out, nor_1_out, not_1_out, not_2_out, not_3_out;
  wire [1:0] counter_1_q_3;
  wire [2:0] counter_1_q_2;
  wire [7:0] counter_2_q, counter_3_q, counter_4_q;
  wire [7:5] counter_1_q;

  Counter counter_1 (
    .Q({counter_1_q, counter_1_q_3, counter_1_q_2}), .clk(clock_1_out), .clr(counter_1_q[5]));  // open: load, D, count, carry, preset, down
  Clock clock_1 (.out(clock_1_out));
  // DipSwitch #(.NSwitches(1)) dipswitch_1: pin names not known
  // DipSwitch #(.NSwitches(1)) dipswitch_2: pin names not known
  // DipSwitch #(.NSwitches(1)) dipswitch_3: pin names not known
  // DipSwitch #(.NSwitches(1)) dipswitch_4: pin names not known
  // DipSwitch #(.NSwitches(1)) dipswitch_5: pin names not known
  // DipSwitch #(.NSwitches(1)) dipswitch_6: pin names not known
  // DipSwitch #(.NSwitches(1)) dipswitch_7: pin names not known
  // DipSwitch #(.NSwitches(1)) dipswitch_8: pin names not known
  Multiplexer #(.select(3), .enable("false")) multiplexer_1 (
    .out(multiplexer_1_out), .sel(counter_1_q_2));  // open: in0, in1, in2, in3, in4, in5, in6, in7
  // DipSwitch #(.NSwitches(1)) dipswitch_9: pin names not known
  // DipSwitch #(.NSwitches(1)) dipswitch_10: pin names not known
  // DipSwitch #(.NSwitches(1)) dipswitch_11: pin names not known
  // DipSwitch #(.NSwitches(1)) dipswitch_12: pin names not known
  // DipSwitch #(.NSwitches(1)) dipswitch_13: pin names not known
  // DipSwitch #(.NSwitches(1)) dipswitch_14: pin names not known
  Multiplexer #(.select(3), .enable("false")) multiplexer_2 (
    .out(multiplexer_2_out), .sel(counter_1_q_2));  // open: in0, in1, in2, in3, in4, in5, in6, in7
  // DipSwitch #(.NSwitches(1)) dipswitch_15: pin names not known
  // DipSwitch #(.NSwitches(1)) dipswitch_16: pin names not known
  // DipSwitch #(.NSwitches(1)) dipswitch_17: pin names not known
  // DipSwitch #(.NSwitches(1)) dipswitch_18: pin names not known
  // DipSwitch #(.NSwitches(1)) dipswitch_19: pin names not known
  // DipSwitch #(.NSwitches(1)) dipswitch_20: pin names not known
  Multiplexer #(.select(2), .enable("false")) multiplexer_3 (
    .in0(multiplexer_1_out), .in1(multiplexer_2_out), .in2(multiplexer_4_out), .in3(multiplexer_5_out),
    .out(multiplexer_3_out), .sel(counter_1_q_3));
  // DipSwitch #(.NSwitches(1)) dipswitch_21: pin names not known
  // DipSwitch #(.NSwitches(1)) dipswitch_22: pin names not known
  // DipSwitch #(.NSwitches(1)) dipswitch_23: pin names not known
  // DipSwitch #(.NSwitches(1)) dipswitch_24: pin names not known
  // DipSwitch #(.NSwitches(1)) dipswitch_25: pin names not known
  // DipSwitch #(.NSwitches(1)) dipswitch_26: pin names not known
  Multiplexer #(.select(3), .enable("false")) multiplexer_4 (
    .out(multiplexer_4_out), .sel(counter_1_q_2));  // open: in0, in1, in2, in3, in4, in5, in6, in7
  // DipSwitch #(.NSwitches(1)) dipswitch_27: pin names not known
  // DipSwitch #(.NSwitches(1)) dipswitch_28: pin names not known
  // DipSwitch #(.NSwitches(1)) dipswitch_29: pin names not known
  // DipSwitch #(.NSwitches(1)) dipswitch_30: pin names not known
  // DipSwitch #(.NSwitches(1)) dipswitch_31: pin names not known
  // DipSwitch #(.NSwitches(1)) dipswitch_32: pin names not known
  Multiplexer #(.select(3), .enable("false")) multiplexer_5 (
    .out(multiplexer_5_out), .sel(counter_1_q_2));  // open: in0, in1, in2, in3, in4, in5, in6, in7
  // DipSwitch #(.NSwitches(1)) dipswitch_33: pin names not known
  // DipSwitch #(.NSwitches(1)) dipswitch_34: pin names not known
  // DipSwitch #(.NSwitches(1)) dipswitch_35: pin names not known
  // DipSwitch #(.NSwitches(1)) dipswitch_36: pin names not known
  Multiplexer #(.select(3), .enable("false")) multiplexer_6 (
    .in0(1'b1), .in5(1'b0), .in6(1'b0), .in7(1'b0), .out(multiplexer_6_out), .sel(counter_1_q_2));  // open: in1, in2, in3, in4
  not not_1 (not_1_out, multiplexer_6_out);
  nor nor_1 (nor_1_out, not_1_out, counter_1_q_3[0], counter_1_q_3[1]);
  LED led_1 (.in(nor_1_out));
  LED led_2 (.in(multiplexer_3_out));
  // DipSwitch #(.NSwitches(8)) dipswitch_37: pin names not known; wires that end beside it: dipswitch_37_p1, dipswitch_37_p2, dipswitch_37_p3, dipswitch_37_p4, dipswitch_37_p5, dipswitch_37_p6, dipswitch_37_p7, dipswitch_37_p8
  Counter counter_2 (
    .Q(counter_2_q), .clk(dipswitch_38_p1), .clr(counter_2_q[5]));  // open: load, D, count, carry, preset, down
  // DipSwitch #(.NSwitches(8)) dipswitch_38: pin names not known; wires that end beside it: dipswitch_38_p1, dipswitch_38_p2, dipswitch_38_p3, dipswitch_38_p4, dipswitch_38_p5, dipswitch_38_p6, dipswitch_38_p7, dipswitch_38_p8, dipswitch_38_p9, dipswitch_38_p10
  Counter counter_3 (
    .Q(counter_3_q), .clk(dipswitch_38_p10), .clr(counter_3_q[5]));  // open: load, D, count, carry, preset, down
  Multiplexer #(.select(3), .enable("false")) multiplexer_7 (
    .in0(1'b1), .in1(dipswitch_37_p8), .in2(1'b0), .in3(1'b1), .in4(dipswitch_37_p7), .in5(1'b0), .in6(1'b1),
    .in7(dipswitch_37_p6), .out(multiplexer_7_out), .sel(counter_2_q[2:0]));
  nand nand_1 (nand_1_out, counter_2_q[0], counter_2_q[1]);
  not not_2 (not_2_out, counter_2_q[2]);
  Multiplexer #(.select(3), .enable("false")) multiplexer_8 (
    .in0(1'b1), .in1(dipswitch_38_p9), .in2(1'b0), .in3(1'b1), .in4(dipswitch_38_p8), .in5(1'b0), .in6(1'b1),
    .in7(dipswitch_38_p7), .out(multiplexer_8_out), .sel(counter_3_q[2:0]));
  Multiplexer #(.select(3), .enable("false")) multiplexer_9 (
    .in0(1'b0), .in1(1'b1), .in2(dipswitch_37_p5), .in3(1'b0), .in4(1'b1), .in5(dipswitch_37_p4), .in6(1'b0),
    .in7(1'b1), .out(multiplexer_9_out), .sel(counter_2_q[2:0]));
  and and_1 (and_1_out, nand_1_out, not_2_out);
  Multiplexer #(.select(3), .enable("false")) multiplexer_10 (
    .in0(1'b0), .in1(1'b1), .in2(dipswitch_38_p6), .in3(1'b0), .in4(1'b1), .in5(dipswitch_38_p5), .in6(1'b0),
    .in7(1'b1), .out(multiplexer_10_out), .sel(counter_3_q[2:0]));
  Multiplexer #(.select(3), .enable("false")) multiplexer_11 (
    .in0(dipswitch_37_p3), .in1(1'b0), .in2(1'b1), .in3(dipswitch_37_p2), .in4(1'b0), .in5(1'b1),
    .in6(dipswitch_37_p1), .in7(1'b0), .out(multiplexer_11_out), .sel(counter_2_q[2:0]));
  Multiplexer #(.select(3), .enable("false")) multiplexer_12 (
    .in0(dipswitch_38_p4), .in1(1'b0), .in2(1'b1), .in3(dipswitch_38_p3), .in4(1'b0), .in5(1'b1),
    .in6(dipswitch_38_p2), .in7(1'b0), .out(multiplexer_12_out), .sel(counter_3_q[2:0]));
  Multiplexer #(.select(2), .enable("false")) multiplexer_13 (
    .in0(multiplexer_7_out), .in1(multiplexer_9_out), .in2(multiplexer_11_out), .in3(and_1_out),
    .out(multiplexer_13_out), .sel(counter_2_q[4:3]));
  Multiplexer #(.select(3), .enable("false")) multiplexer_14 (
    .in0(1'b1), .in1(1'b1), .in2(1'b1), .in3(1'b0), .in4(1'b0), .in5(1'b0), .in6(1'b0), .in7(1'b0),
    .out(multiplexer_14_out), .sel(counter_3_q[2:0]));
  Multiplexer #(.select(2), .enable("false")) multiplexer_15 (
    .in0(multiplexer_8_out), .in1(multiplexer_10_out), .in2(multiplexer_12_out), .in3(multiplexer_14_out),
    .out(multiplexer_15_out), .sel(counter_3_q[4:3]));
  LED led_3 (.in(multiplexer_13_out));
  LED led_4 (.in(multiplexer_15_out));
  // DipSwitch #(.NSwitches(8)) dipswitch_39: pin names not known; wires that end beside it: dipswitch_39_p1, dipswitch_39_p2, dipswitch_39_p3, dipswitch_39_p4, dipswitch_39_p5, dipswitch_39_p6, dipswitch_39_p7, dipswitch_39_p8, dipswitch_39_p9
  Counter counter_4 (
    .Q(counter_4_q), .clk(dipswitch_39_p9), .clr(counter_4_q[5]));  // open: load, D, count, carry, preset, down
  Button button_1 (.out(button_1_out));
  Multiplexer #(.select(3), .enable("false")) multiplexer_16 (
    .in0(1'b1), .in1(dipswitch_39_p8), .in2(1'b0), .in3(1'b1), .in4(dipswitch_39_p7), .in5(1'b0), .in6(1'b1),
    .in7(dipswitch_39_p6), .out(multiplexer_16_out), .sel(counter_4_q[2:0]));
  Multiplexer #(.select(3), .enable("false")) multiplexer_17 (
    .in0(1'b0), .in1(1'b1), .in2(dipswitch_39_p5), .in3(1'b0), .in4(1'b1), .in5(dipswitch_39_p4), .in6(1'b0),
    .in7(1'b1), .out(multiplexer_17_out), .sel(counter_4_q[2:0]));
  Multiplexer #(.select(3), .enable("false")) multiplexer_18 (
    .in0(dipswitch_39_p3), .in1(1'b0), .in2(1'b1), .in3(dipswitch_39_p2), .in4(1'b0), .in5(1'b1),
    .in6(dipswitch_39_p1), .in7(1'b0), .out(multiplexer_18_out), .sel(counter_4_q[2:0]));
  Multiplexer #(.select(2), .enable("false")) multiplexer_19 (
    .in0(1'b1), .in1(1'b1), .in2(1'b1), .in3(1'b0), .out(multiplexer_19_out), .sel(counter_4_q[1:0]));
  and and_2 (and_2_out, multiplexer_19_out, not_3_out);
  not not_3 (not_3_out, counter_4_q[2]);
  Multiplexer #(.select(2), .enable("false")) multiplexer_20 (
    .in0(multiplexer_16_out), .in1(multiplexer_17_out), .in2(multiplexer_18_out), .in3(and_2_out),
    .out(multiplexer_20_out), .sel(counter_4_q[4:3]));
  LED led_5 (.in(multiplexer_20_out));

  // Notes on the sheet:
  //   clock
  //   controller 1
  //   controller 2
  //   controller 3
  //   controller 4
  //   sync bit logic
  //   sync output
  //   data output
endmodule
