// Logisim project demuxer.circ as structural Verilog: 1 circuit, main circuit main
module main (
);

  wire and_1_out, and_2_out, clock_1_out, clock_2_out, clock_3_out, digital_oscilloscope_1_p3,
       dipswitch_1_p1, dipswitch_1_p2, dipswitch_1_p3, dipswitch_1_p4, dipswitch_1_p5, dipswitch_1_p6,
       dipswitch_1_p7, dipswitch_1_p8, dipswitch_2_p1, dipswitch_2_p2, dipswitch_2_p3, dipswitch_2_p4,
       dipswitch_2_p5, dipswitch_2_p6, dipswitch_2_p7, dipswitch_2_p8, dipswitch_3_p1, dipswitch_3_p2,
       dipswitch_3_p3, dipswitch_3_p4, dipswitch_3_p5, dipswitch_3_p6, dipswitch_3_p7, dipswitch_3_p8,
       multiplexer_1_out, multiplexer_2_out, multiplexer_3_out, multiplexer_4_out, multiplexer_5_out,
       multiplexer_6_out, multiplexer_7_out, multiplexer_8_out, multiplexer_9_out, multiplexer_10_out,
       multiplexer_11_out, multiplexer_12_out, multiplexer_13_out, multiplexer_14_out, nand_1_out, not_1_out,
       not_2_out;
  wire [1:0] counter_3_q_2;
  wire [7:0] counter_1_q, counter_2_q;
  wire [7:2] counter_3_q;

  // DipSwitch #(.NSwitches(8)) dipswitch_1: pin names not known; wires that end beside it: dipswitch_1_p1, dipswitch_1_p2, dipswitch_1_p3, dipswitch_1_p4, dipswitch_1_p5, dipswitch_1_p6, dipswitch_1_p7, dipswitch_1_p8
  Counter counter_1 (
    .Q(counter_1_q), .clk(clock_1_out), .clr(counter_1_q[5]));  // open: load, D, count, carry, preset, down
  Clock clock_1 (.out(clock_1_out));
  // DipSwitch #(.NSwitches(8)) dipswitch_2: pin names not known; wires that end beside it: dipswitch_2_p1, dipswitch_2_p2, dipswitch_2_p3, dipswitch_2_p4, dipswitch_2_p5, dipswitch_2_p6, dipswitch_2_p7, dipswitch_2_p8
  Counter counter_2 (
    .Q(counter_2_q), .clk(clock_2_out), .clr(counter_2_q[5]));  // open: load, D, count, carry, preset, down
  Clock clock_2 (.out(clock_2_out));
  Multiplexer #(.select(3), .enable("false")) multiplexer_1 (
    .in0(1'b1), .in1(dipswitch_1_p8), .in2(1'b0), .in3(1'b1), .in4(dipswitch_1_p7), .in5(1'b0), .in6(1'b1),
    .in7(dipswitch_1_p6), .out(multiplexer_1_out), .sel(counter_1_q[2:0]));
  nand nand_1 (nand_1_out, counter_1_q[0], counter_1_q[1]);
  not not_1 (not_1_out, counter_1_q[2]);
  Multiplexer #(.select(3), .enable("false")) multiplexer_2 (
    .in0(1'b1), .in1(dipswitch_2_p8), .in2(1'b0), .in3(1'b1), .in4(dipswitch_2_p7), .in5(1'b0), .in6(1'b1),
    .in7(dipswitch_2_p6), .out(multiplexer_2_out), .sel(counter_2_q[2:0]));
  Multiplexer #(.select(3), .enable("false")) multiplexer_3 (
    .in0(1'b0), .in1(1'b1), .in2(dipswitch_1_p5), .in3(1'b0), .in4(1'b1), .in5(dipswitch_1_p4), .in6(1'b0),
    .in7(1'b1), .out(multiplexer_3_out), .sel(counter_1_q[2:0]));
  and and_1 (and_1_out, nand_1_out, not_1_out);
  Multiplexer #(.select(3), .enable("false")) multiplexer_4 (
    .in0(1'b0), .in1(1'b1), .in2(dipswitch_2_p5), .in3(1'b0), .in4(1'b1), .in5(dipswitch_2_p4), .in6(1'b0),
    .in7(1'b1), .out(multiplexer_4_out), .sel(counter_2_q[2:0]));
  Multiplexer #(.select(3), .enable("false")) multiplexer_5 (
    .in0(dipswitch_1_p3), .in1(1'b0), .in2(1'b1), .in3(dipswitch_1_p2), .in4(1'b0), .in5(1'b1),
    .in6(dipswitch_1_p1), .in7(1'b0), .out(multiplexer_5_out), .sel(counter_1_q[2:0]));
  Multiplexer #(.select(2), .enable("false")) multiplexer_6 (
    .in0(multiplexer_1_out), .in1(multiplexer_3_out), .in2(multiplexer_5_out), .in3(and_1_out),
    .out(multiplexer_6_out), .sel(counter_1_q[4:3]));
  Multiplexer #(.select(3), .enable("false")) multiplexer_7 (
    .in0(dipswitch_2_p3), .in1(1'b0), .in2(1'b1), .in3(dipswitch_2_p2), .in4(1'b0), .in5(1'b1),
    .in6(dipswitch_2_p1), .in7(1'b0), .out(multiplexer_7_out), .sel(counter_2_q[2:0]));
  Multiplexer #(.select(3), .enable("false")) multiplexer_8 (
    .in0(1'b1), .in1(1'b1), .in2(1'b1), .in3(1'b0), .in4(1'b0), .in5(1'b0), .in6(1'b0), .in7(1'b0),
    .out(multiplexer_8_out), .sel(counter_2_q[2:0]));
  Multiplexer #(.select(2), .enable("false")) multiplexer_9 (
    .in0(multiplexer_2_out), .in1(multiplexer_4_out), .in2(multiplexer_7_out), .in3(multiplexer_8_out),
    .out(multiplexer_9_out), .sel(counter_2_q[4:3]));
  LED led_1 (.in(multiplexer_6_out));
  LED led_2 (.in(multiplexer_9_out));
  // DipSwitch #(.NSwitches(8)) dipswitch_3: pin names not known; wires that end beside it: dipswitch_3_p1, dipswitch_3_p2, dipswitch_3_p3, dipswitch_3_p4, dipswitch_3_p5, dipswitch_3_p6, dipswitch_3_p7, dipswitch_3_p8
  Clock clock_3 (.out(clock_3_out));
  // Digital_Oscilloscope #(.nState(35)) digital_oscilloscope_1: pin names not known; wires that end beside it: clock_2_out, multiplexer_9_out, digital_oscilloscope_1_p3
  Button button_1 (.out(digital_oscilloscope_1_p3));
  Multiplexer #(.select(3), .enable("false")) multiplexer_10 (
    .in0(1'b1), .in1(dipswitch_3_p8), .in2(1'b0), .in3(1'b1), .in4(dipswitch_3_p7), .in5(1'b0), .in6(1'b1),
    .in7(dipswitch_3_p6), .out(multiplexer_10_out), .sel({counter_3_q[2], counter_3_q_2}));
  Counter counter_3 (
    .Q({counter_3_q, counter_3_q_2}), .clk(clock_3_out), .clr(counter_3_q[5]));  // open: load, D, count, carry, preset, down
  Multiplexer #(.select(3), .enable("false")) multiplexer_11 (
    .in0(1'b0), .in1(1'b1), .in2(dipswitch_3_p5), .in3(1'b0), .in4(1'b1), .in5(dipswitch_3_p4), .in6(1'b0),
    .in7(1'b1), .out(multiplexer_11_out), .sel({counter_3_q[2], counter_3_q_2}));
  Multiplexer #(.select(3), .enable("false")) multiplexer_12 (
    .in0(dipswitch_3_p3), .in1(1'b0), .in2(1'b1), .in3(dipswitch_3_p2), .in4(1'b0), .in5(1'b1),
    .in6(dipswitch_3_p1), .in7(1'b0), .out(multiplexer_12_out), .sel({counter_3_q[2], counter_3_q_2}));
  Multiplexer #(.select(2), .enable("false")) multiplexer_13 (
    .in0(1'b1), .in1(1'b1), .in2(1'b1), .in3(1'b0), .out(multiplexer_13_out), .sel(counter_3_q_2));
  and and_2 (and_2_out, multiplexer_13_out, not_2_out);
  not not_2 (not_2_out, counter_3_q[2]);
  Multiplexer #(.select(2), .enable("false")) multiplexer_14 (
    .in0(multiplexer_10_out), .in1(multiplexer_11_out), .in2(multiplexer_12_out), .in3(and_2_out),
    .out(multiplexer_14_out), .sel(counter_3_q[4:3]));
  LED led_3 (.in(multiplexer_14_out));
endmodule
